# Fritzing sketch LittleG (saved by Fritzing 0.9.2b)
perfboards: 1

parts:
  Part2 = Arduino Uno (Rev3)
  J3 = female pin header, 8 pins [form="♀ (female)"]
  S2 = Pushbutton [package="[THT]"]
  R2 = Resistor [tolerance=±5% resistance=220 package=THT]
  LED1 = LED - 5mm [color="Green (555nm)" package="5 mm [THT]"]
  J4 = female pin header, 6 pins [form="♀ (female)"]
  R3 = Resistor [tolerance=±5% resistance=220 package=THT]
  LED2 = LED - 5mm [color="Red (633nm)" package="5 mm [THT]"]
  J5 = male pin header, 3 pins [form="♂ (male)"]
  U1 = mystery part, 3 pins [chip_label=ESC]
  U2 = mystery part, 2 pins [chip_label=LED]  # not connected

nets:
  N1: Part2.D10_PWM/SS, J3.pin6
  N2: Part2.D11_PWM/MOSI, J3.pin5
  N3: Part2.D12/MISO, J3.pin4
  N4: Part2.D13/SCK, J3.pin3
  N5: Part2.GND, J3.pin2
  N6: S2.Pin_1, S2.Pin_2, LED1.cathode, J4.pin5
  N7: S2.Pin_3, S2.Pin_4
  N8: R2.Pin_1, LED1.anode
  N9: R3.Pin_0, LED2.anode
  N10: J5.pin1, U1.pin1
  N11: J5.pin2, U1.pin2
  N12: J5.pin3, U1.pin3

notes:
  To SpokePOV boards
  From ESC BEC
  Adafruit Protoshield for Arduino
  via Adafruit Slip Ring
  NOTE:  +5V from the BEC does not
  connect to the Arduino!  It connects
  directly to the SpokePOV boards.
  USB to Computer
  for Arduino power
  and serial data
